// Logisim project GuessTheNumber.circ as structural Verilog: 5 circuits, main circuit Game
module Game (
  input  [3:0] chute,
  input  confirmar
);

  wire and_1_out, comparador_saida_comparador, decodificador_a, decodificador_b, decodificador_c,
       decodificador_d, decodificador_e, decodificador_f, decodificador_g, new_out;
  wire [3:0] diferenca_saida_diferenca, random_1_out, register_1_q;
  wire [7:0] cores_blue, cores_red;

  Button \new  (.out(new_out));
  Random #(.width(4)) random_1 (.clk(new_out), .out(random_1_out));  // open: next, clr
  Register #(.width(4), .Select("low")) register_1 (
    .D(random_1_out), .Q(register_1_q), .clk(new_out));  // open: en, clr
  Decodificador decodificador (
    .E3(chute[3]), .E2(chute[2]), .E1(chute[1]), .E0(chute[0]), .a(decodificador_a), .b(decodificador_b),
    .c(decodificador_c), .d(decodificador_d), .e(decodificador_e), .f(decodificador_f), .g(decodificador_g));
  Diferenca diferenca (.chute(chute), .aleatorio(register_1_q), .saida_diferenca(diferenca_saida_diferenca));
  _7_Segment_Display u_7_segment_display_1 (
    .g(decodificador_g), .f(decodificador_f), .a(decodificador_a), .b(decodificador_b), .e(decodificador_e),
    .d(decodificador_d), .c(decodificador_c));  // open: dp
  Cores cores (.diferenca_in(diferenca_saida_diferenca), .blue(cores_blue), .red(cores_red));
  Comparador comparador (.chute(chute), .aleatorio(register_1_q), .saida_comparador(comparador_saida_comparador));
  // RGBLed #(.multibit("true")) rgbled_1: pin names not known; wires that end beside it: cores_blue, {8{1'b0}}, cores_red
  and and_1 (and_1_out, comparador_saida_comparador, confirmar);
  LED acertou (.in(and_1_out));
endmodule

module Comparador (
  input  [3:0] chute,
  input  [3:0] aleatorio,
  output saida_comparador
);

  wire xnor_1_out, xnor_2_out, xnor_3_out, xnor_4_out;

  xnor xnor_1 (xnor_1_out, chute[0], aleatorio[0]);
  xnor xnor_2 (xnor_2_out, chute[1], aleatorio[1]);
  xnor xnor_3 (xnor_3_out, chute[2], aleatorio[2]);
  xnor xnor_4 (xnor_4_out, chute[3], aleatorio[3]);
  and and_1 (saida_comparador, xnor_1_out, xnor_2_out, xnor_3_out, xnor_4_out);
endmodule

module Diferenca (
  input  [3:0] chute,
  input  [3:0] aleatorio,
  output [3:0] saida_diferenca
);

  wire comparator_1_gt;
  wire [3:0] subtractor_1_out, subtractor_2_out;

  Comparator #(.width(4)) comparator_1 (.a(chute), .b(aleatorio), .gt(comparator_1_gt));  // open: eq, lt
  Subtractor #(.width(4)) subtractor_1 (.a(chute), .b(aleatorio), .out(subtractor_1_out));  // open: bin, bout
  Subtractor #(.width(4)) subtractor_2 (.a(aleatorio), .b(chute), .out(subtractor_2_out));  // open: bin, bout
  Multiplexer #(.width(4), .enable("false")) multiplexer_1 (
    .in0(subtractor_2_out), .in1(subtractor_1_out), .out(saida_diferenca), .sel(comparator_1_gt));
endmodule

module Decodificador (
  input  E3,
  input  E2,
  input  E1,
  input  E0,
  output a,
  output b,
  output c,
  output d,
  output e,
  output f,
  output g
);

  wire and_1_out, and_2_out, and_3_out, and_4_out, and_5_out, and_6_out, and_7_out, and_8_out, and_9_out,
       and_10_out, and_11_out, and_12_out, and_13_out, and_14_out, and_15_out, and_16_out, and_17_out,
       and_18_out, and_19_out, and_20_out, and_21_out, and_22_out, and_23_out, and_24_out, and_25_out,
       and_26_out, and_27_out, and_28_out, and_29_out, and_30_out, and_31_out, and_32_out, and_33_out,
       and_34_out, and_35_out, not_1_out, not_2_out, not_3_out, not_4_out, not_5_out, not_6_out, not_7_out,
       not_8_out, not_9_out, not_10_out, not_11_out, not_12_out, not_13_out, not_14_out, not_15_out,
       not_16_out, not_17_out, not_18_out, not_19_out, not_20_out, not_21_out, not_22_out, not_23_out,
       not_24_out, not_25_out, not_26_out, not_27_out, not_28_out, not_29_out, not_30_out, not_31_out,
       not_32_out, not_33_out, not_34_out, not_35_out, not_36_out, not_37_out, not_38_out, not_39_out,
       not_40_out, not_41_out, not_42_out, not_43_out;

  not not_1 (not_1_out, E2);
  and and_1 (and_1_out, not_1_out, not_2_out);
  not not_2 (not_2_out, E0);
  not not_3 (not_3_out, E3);
  and and_2 (and_2_out, not_3_out, E1);
  not not_4 (not_4_out, E3);
  and and_3 (and_3_out, not_4_out, E2, E0);
  and and_4 (and_4_out, E2, E1);
  and and_5 (and_5_out, E3, not_5_out, not_6_out);
  not not_5 (not_5_out, E2);
  not not_6 (not_6_out, E1);
  and and_6 (and_6_out, E3, not_7_out);
  not not_7 (not_7_out, E0);
  not not_8 (not_8_out, E3);
  and and_7 (and_7_out, not_8_out, not_9_out);
  not not_9 (not_9_out, E2);
  not not_10 (not_10_out, E3);
  not not_11 (not_11_out, E1);
  and and_8 (and_8_out, not_10_out, not_11_out, not_12_out);
  not not_12 (not_12_out, E0);
  not not_13 (not_13_out, E2);
  and and_9 (and_9_out, not_13_out, not_14_out);
  not not_14 (not_14_out, E0);
  not not_15 (not_15_out, E3);
  and and_10 (and_10_out, not_15_out, E1, E0);
  not not_16 (not_16_out, E1);
  and and_11 (and_11_out, E3, not_16_out, E0);
  not not_17 (not_17_out, E3);
  and and_12 (and_12_out, not_17_out, not_18_out);
  not not_18 (not_18_out, E1);
  not not_19 (not_19_out, E3);
  and and_13 (and_13_out, not_19_out, E0);
  not not_20 (not_20_out, E1);
  and and_14 (and_14_out, not_20_out, E0);
  not not_21 (not_21_out, E3);
  and and_15 (and_15_out, not_21_out, E2);
  and and_16 (and_16_out, E3, not_22_out);
  not not_22 (not_22_out, E2);
  not not_23 (not_23_out, E3);
  not not_24 (not_24_out, E2);
  and and_17 (and_17_out, not_23_out, not_24_out, not_25_out);
  not not_25 (not_25_out, E0);
  not not_26 (not_26_out, E2);
  and and_18 (and_18_out, not_26_out, E1, E0);
  and and_19 (and_19_out, E2, not_27_out, E0);
  not not_27 (not_27_out, E1);
  and and_20 (and_20_out, E2, E1, not_28_out);
  not not_28 (not_28_out, E0);
  and and_21 (and_21_out, E3, not_29_out);
  not not_29 (not_29_out, E1);
  not not_30 (not_30_out, E2);
  and and_22 (and_22_out, not_30_out, not_31_out);
  not not_31 (not_31_out, E0);
  and and_23 (and_23_out, E1, not_32_out);
  not not_32 (not_32_out, E0);
  and and_24 (and_24_out, E3, E1);
  and and_25 (and_25_out, E3, E2);
  not not_33 (not_33_out, E1);
  and and_26 (and_26_out, not_33_out, not_34_out);
  not not_34 (not_34_out, E0);
  not not_35 (not_35_out, E3);
  and and_27 (and_27_out, not_35_out, E2, not_36_out);
  not not_36 (not_36_out, E1);
  and and_28 (and_28_out, E2, not_37_out);
  not not_37 (not_37_out, E0);
  and and_29 (and_29_out, E3, not_38_out);
  not not_38 (not_38_out, E2);
  and and_30 (and_30_out, E3, E1);
  not not_39 (not_39_out, E2);
  and and_31 (and_31_out, not_39_out, E1);
  and and_32 (and_32_out, E1, not_40_out);
  not not_40 (not_40_out, E0);
  not not_41 (not_41_out, E3);
  and and_33 (and_33_out, not_41_out, E2, not_42_out);
  not not_42 (not_42_out, E1);
  and and_34 (and_34_out, E3, not_43_out);
  not not_43 (not_43_out, E2);
  and and_35 (and_35_out, E3, E0);
  or or_1 (b, and_7_out, and_8_out, and_9_out, and_10_out, and_11_out);
  or or_2 (c, and_12_out, and_13_out, and_14_out, and_15_out, and_16_out);
  or or_3 (d, and_17_out, and_18_out, and_19_out, and_20_out, and_21_out);
  or or_4 (e, and_22_out, and_23_out, and_24_out, and_25_out);
  or or_5 (f, and_26_out, and_27_out, and_28_out, and_29_out, and_30_out);
  or or_6 (g, and_31_out, and_32_out, and_33_out, and_34_out, and_35_out);
  or or_7 (a, and_1_out, and_2_out, and_3_out, and_4_out, and_5_out, and_6_out);
endmodule

module Cores (
  input  [3:0] diferenca_in,
  output [7:0] blue,
  output [7:0] red
);

  assign red[7:4] = ~diferenca_in;  // NOT_Gate not_1, 4 bits wide

  assign blue = {diferenca_in, 4'b0000};
  assign red[3:0] = 4'b0000;
endmodule
